// Logisim project scdp1.circ as structural Verilog: 12 circuits, main circuit WritePort
// 32
module main (
  output out_1,
  output out_2,
  output [31:0] out_3,
  output [31:0] out_4,
  output [31:0] out_5,
  output out_6,
  output out_7,
  output out_8,
  output out_9,
  output out_10,
  output out_11,
  output out_12,
  output out_13,
  output out_14,
  output out_15
);

  wire clock_1_out, clock_2_out, clock_3_out, clock_4_out, clock_5_out;
  wire [2:0] alu_cu_1_out_3;
  wire [3:0] alu_1_aluresult, alu_1_aluresult_2, alu_1_aluresult_4, alu_1_aluresult_5, alu_1_aluresult_6,
       alu_1_aluresult_7, alu_1_aluresult_8;
  wire [11:8] alu_1_aluresult_3;
  wire [31:0] instruction_fetch_module_1_ir, instruction_fetch_module_2_ir, instruction_fetch_module_3_ir,
       readport_2_readdata_1, readport_2_readdata_2, readport_3_readdata_1, readport_3_readdata_2;

  Clock clock_1 (.out(clock_1_out));
  Clock clock_2 (.out(clock_2_out));
  Clock clock_3 (.out(clock_3_out));
  Instruction_Fetch_Module instruction_fetch_module_1 (
    .Clock(clock_1_out), .Enable(1'b1), .IR(instruction_fetch_module_1_ir));
  WritePort writeport_1 (.Write(1'b1), .Clock(clock_2_out), .WriteReg(5'b00001), .WriteData({32{1'b1}}));
  Instruction_Fetch_Module instruction_fetch_module_2 (
    .Clock(clock_3_out), .Enable(1'b1), .IR(instruction_fetch_module_2_ir));
  ALU_CU alu_cu_1 (.ALUOP(2'b10), .FC(6'b100100), .out_3(alu_cu_1_out_3));
  Register #(.width(32)) register_1 (.D(instruction_fetch_module_2_ir), .clk(clock_3_out));  // open: en, Q, clr
  ReadPort readport_1 (
    .Read_Reg1(instruction_fetch_module_1_ir[25:21]), .Read_Reg2(instruction_fetch_module_1_ir[20:16]),
    .Write(1'b1), .Clock(clock_1_out), .WriteReg(instruction_fetch_module_1_ir[15:11]), .WriteData(32'ha),
    .ReadData_1(out_3), .ReadData_2(out_5));
  // Probe on alu_cu_1_out_3
  Hex_Digit_Display hex_digit_display_1 (.value(alu_1_aluresult_8));  // open: dp
  Clock clock_4 (.out(clock_4_out));
  Clock clock_5 (.out(clock_5_out));
  Hex_Digit_Display hex_digit_display_2 (.value(alu_1_aluresult_7));  // open: dp
  ALU alu_1 (
    .ALUOperation(3'b000), .SRC1(32'h12), .SRC2(32'ha), .ZF(out_1),
    .ALUResult({alu_1_aluresult_8, alu_1_aluresult_7, alu_1_aluresult_6, alu_1_aluresult_5, alu_1_aluresult_4, alu_1_aluresult_3, alu_1_aluresult_2, alu_1_aluresult}));
  Instruction_Fetch_Module instruction_fetch_module_3 (
    .Clock(clock_4_out), .Enable(1'b1), .IR(instruction_fetch_module_3_ir));
  Hex_Digit_Display hex_digit_display_3 (.value(alu_1_aluresult_5));  // open: dp
  Hex_Digit_Display hex_digit_display_4 (.value(alu_1_aluresult_6));  // open: dp
  Main_CU main_cu_1 (
    .OPCODES(6'b100011), .RegWrite(out_6), .RegDst(out_7), .ALUsrc(out_8), .MemtoReg(out_10),
    .MemRead(out_13), .MemWrite(out_14), .Branch(out_15), .Jump(out_12), .ALUOp1(out_11), .ALUOp0(out_9));
  ReadPort readport_2 (
    .Read_Reg1({5{1'b0}}), .Read_Reg2(5'b00100), .Write(1'b1), .Clock(clock_5_out), .WriteReg(5'b00100),
    .WriteData(32'h2145), .ReadData_1(readport_2_readdata_1), .ReadData_2(readport_2_readdata_2));
  Hex_Digit_Display hex_digit_display_5 (.value(alu_1_aluresult_4));  // open: dp
  ReadPort readport_3 (
    .Read_Reg1(instruction_fetch_module_3_ir[25:21]), .Read_Reg2(instruction_fetch_module_3_ir[20:16]),
    .Write(1'b1), .Clock(clock_4_out), .WriteReg(instruction_fetch_module_3_ir[15:11]), .WriteData(32'ha),
    .ReadData_1(readport_3_readdata_1), .ReadData_2(readport_3_readdata_2));
  // Probe on readport_2_readdata_1
  // Probe on readport_2_readdata_2
  Hex_Digit_Display hex_digit_display_6 (.value(alu_1_aluresult_3));  // open: dp
  ALU alu_2 (
    .ALUOperation(3'b000), .SRC1(readport_3_readdata_1), .SRC2(readport_3_readdata_2), .ZF(out_2),
    .ALUResult(out_4));
  Hex_Digit_Display hex_digit_display_7 (.value(alu_1_aluresult_2));  // open: dp
  Hex_Digit_Display hex_digit_display_8 (.value(alu_1_aluresult));  // open: dp

  // Notes on the sheet:
  //   WriteData
  //   Clock
  //   Enable
  //   WriteReg
  //   Clock
  //   Enable
  //   Write
  //   Clock
  //   REGISTER FILE WRITE PORT SIMULATION
  //   SIMULATING INSTRUCTION FETCH
  //   ALU CU WORKING
  //   SIMULATING INSTRUCTION FETCH WITH REGISTER FILE
  //   IR
  //   ReadData 1
  //   ReadData 2
  //   WriteData
  //   Clock
  //   Clock
  //   WriteReg
  //   ReadReg 1
  //   ReadReg 2
  //   Write
  //   SIMULATING COMPLETE REGISTER FILE 
  //   SIMULATING ALU
  //   SIMULATING INSTRUCTION FETCH WITH REGISTER FILE
  //   MAIN CU WORKING
  //   ReadData 1
  //   ReadData 2
endmodule

// Reg_wp
module WritePort (
  input  Write,
  input  Clock,
  input  [4:0] WriteReg,
  input  [31:0] WriteData
);

  wire and_1_out, and_2_out, and_3_out, and_4_out, and_5_out, and_6_out, and_7_out, and_8_out, and_9_out,
       and_10_out, and_11_out, and_12_out, and_13_out, and_14_out, and_15_out, and_16_out, and_17_out,
       and_18_out, and_19_out, and_20_out, and_21_out, and_22_out, and_23_out, and_24_out, and_25_out,
       and_26_out, and_27_out, and_28_out, and_29_out, and_30_out, and_31_out, and_32_out, decoder_1_out0,
       decoder_1_out1, decoder_1_out2, decoder_1_out3, decoder_1_out4, decoder_1_out5, decoder_1_out6,
       decoder_1_out7, decoder_1_out8, decoder_1_out9, decoder_1_out10, decoder_1_out11, decoder_1_out12,
       decoder_1_out13, decoder_1_out14, decoder_1_out15, decoder_1_out16, decoder_1_out17, decoder_1_out18,
       decoder_1_out19, decoder_1_out20, decoder_1_out21, decoder_1_out22, decoder_1_out23, decoder_1_out24,
       decoder_1_out25, decoder_1_out26, decoder_1_out27, decoder_1_out28, decoder_1_out29, decoder_1_out30,
       decoder_1_out31;

  Decoder #(.select(5), .enable("false")) decoder_1 (
    .out0(decoder_1_out0), .out1(decoder_1_out1), .out2(decoder_1_out2), .out3(decoder_1_out3),
    .out4(decoder_1_out4), .out5(decoder_1_out5), .out6(decoder_1_out6), .out7(decoder_1_out7),
    .out8(decoder_1_out8), .out9(decoder_1_out9), .out10(decoder_1_out10), .out11(decoder_1_out11),
    .out12(decoder_1_out12), .out13(decoder_1_out13), .out14(decoder_1_out14), .out15(decoder_1_out15),
    .out16(decoder_1_out16), .out17(decoder_1_out17), .out18(decoder_1_out18), .out19(decoder_1_out19),
    .out20(decoder_1_out20), .out21(decoder_1_out21), .out22(decoder_1_out22), .out23(decoder_1_out23),
    .out24(decoder_1_out24), .out25(decoder_1_out25), .out26(decoder_1_out26), .out27(decoder_1_out27),
    .out28(decoder_1_out28), .out29(decoder_1_out29), .out30(decoder_1_out30), .out31(decoder_1_out31),
    .sel(WriteReg));
  and and_1 (and_1_out, Write, decoder_1_out0);
  and and_2 (and_2_out, Write, decoder_1_out1);
  and and_3 (and_3_out, Write, decoder_1_out2);
  and and_4 (and_4_out, Write, decoder_1_out3);
  and and_5 (and_5_out, Write, decoder_1_out4);
  and and_6 (and_6_out, Write, decoder_1_out5);
  and and_7 (and_7_out, Write, decoder_1_out6);
  and and_8 (and_8_out, Write, decoder_1_out7);
  and and_9 (and_9_out, Write, decoder_1_out8);
  and and_10 (and_10_out, Write, decoder_1_out9);
  and and_11 (and_11_out, Write, decoder_1_out10);
  and and_12 (and_12_out, Write, decoder_1_out11);
  and and_13 (and_13_out, Write, decoder_1_out12);
  and and_14 (and_14_out, Write, decoder_1_out13);
  and and_15 (and_15_out, Write, decoder_1_out14);
  and and_16 (and_16_out, Write, decoder_1_out15);
  and and_17 (and_17_out, Write, decoder_1_out16);
  and and_18 (and_18_out, Write, decoder_1_out17);
  and and_19 (and_19_out, Write, decoder_1_out18);
  and and_20 (and_20_out, Write, decoder_1_out19);
  and and_21 (and_21_out, Write, decoder_1_out20);
  and and_22 (and_22_out, Write, decoder_1_out21);
  and and_23 (and_23_out, Write, decoder_1_out22);
  and and_24 (and_24_out, Write, decoder_1_out23);
  and and_25 (and_25_out, Write, decoder_1_out24);
  and and_26 (and_26_out, Write, decoder_1_out25);
  and and_27 (and_27_out, Write, decoder_1_out26);
  and and_28 (and_28_out, Write, decoder_1_out27);
  and and_29 (and_29_out, Write, decoder_1_out28);
  and and_30 (and_30_out, Write, decoder_1_out29);
  and and_31 (and_31_out, Write, decoder_1_out30);
  and and_32 (and_32_out, Write, decoder_1_out31);
  Register #(.width(32)) _0 (.D(WriteData), .en(and_1_out), .clk(Clock));  // open: Q, clr
  Register #(.width(32)) _1 (.D(WriteData), .en(and_2_out), .clk(Clock));  // open: Q, clr
  Register #(.width(32)) _2 (.D(WriteData), .en(and_3_out), .clk(Clock));  // open: Q, clr
  Register #(.width(32)) _3 (.D(WriteData), .en(and_4_out), .clk(Clock));  // open: Q, clr
  Register #(.width(32)) _4 (.D(WriteData), .en(and_5_out), .clk(Clock));  // open: Q, clr
  Register #(.width(32)) _5 (.D(WriteData), .en(and_6_out), .clk(Clock));  // open: Q, clr
  Register #(.width(32)) _6 (.D(WriteData), .en(and_7_out), .clk(Clock));  // open: Q, clr
  Register #(.width(32)) _7 (.D(WriteData), .en(and_8_out), .clk(Clock));  // open: Q, clr
  Register #(.width(32)) _8 (.D(WriteData), .en(and_9_out), .clk(Clock));  // open: Q, clr
  Register #(.width(32)) _9 (.D(WriteData), .en(and_10_out), .clk(Clock));  // open: Q, clr
  Register #(.width(32)) _10 (.D(WriteData), .en(and_11_out), .clk(Clock));  // open: Q, clr
  Register #(.width(32)) _11 (.D(WriteData), .en(and_12_out), .clk(Clock));  // open: Q, clr
  Register #(.width(32)) _12 (.D(WriteData), .en(and_13_out), .clk(Clock));  // open: Q, clr
  Register #(.width(32)) _13 (.D(WriteData), .en(and_14_out), .clk(Clock));  // open: Q, clr
  Register #(.width(32)) _14 (.D(WriteData), .en(and_15_out), .clk(Clock));  // open: Q, clr
  Register #(.width(32)) _15 (.D(WriteData), .en(and_16_out), .clk(Clock));  // open: Q, clr
  Register #(.width(32)) _16 (.D(WriteData), .en(and_17_out), .clk(Clock));  // open: Q, clr
  Register #(.width(32)) _17 (.D(WriteData), .en(and_18_out), .clk(Clock));  // open: Q, clr
  Register #(.width(32)) _18 (.D(WriteData), .en(and_19_out), .clk(Clock));  // open: Q, clr
  Register #(.width(32)) _19 (.D(WriteData), .en(and_20_out), .clk(Clock));  // open: Q, clr
  Register #(.width(32)) _20 (.D(WriteData), .en(and_21_out), .clk(Clock));  // open: Q, clr
  Register #(.width(32)) _21 (.D(WriteData), .en(and_22_out), .clk(Clock));  // open: Q, clr
  Register #(.width(32)) _22 (.D(WriteData), .en(and_23_out), .clk(Clock));  // open: Q, clr
  Register #(.width(32)) _23 (.D(WriteData), .en(and_24_out), .clk(Clock));  // open: Q, clr
  Register #(.width(32)) _24 (.D(WriteData), .en(and_25_out), .clk(Clock));  // open: Q, clr
  Register #(.width(32)) _25 (.D(WriteData), .en(and_26_out), .clk(Clock));  // open: Q, clr
  Register #(.width(32)) _26 (.D(WriteData), .en(and_27_out), .clk(Clock));  // open: Q, clr
  Register #(.width(32)) _27 (.D(WriteData), .en(and_28_out), .clk(Clock));  // open: Q, clr
  Register #(.width(32)) _28 (.D(WriteData), .en(and_29_out), .clk(Clock));  // open: Q, clr
  Register #(.width(32)) _29 (.D(WriteData), .en(and_30_out), .clk(Clock));  // open: Q, clr
  Register #(.width(32)) _30 (.D(WriteData), .en(and_31_out), .clk(Clock));  // open: Q, clr
  Register #(.width(32)) _31 (.D(WriteData), .en(and_32_out), .clk(Clock));  // open: Q, clr
endmodule

// RegFile
module ReadPort (
  input  [4:0] Read_Reg1,
  input  [4:0] Read_Reg2,
  input  Write,
  input  Clock,
  input  [4:0] WriteReg,
  input  [31:0] WriteData,
  output [31:0] ReadData_1,
  output [31:0] ReadData_2
);

  wire and_1_out, and_2_out, and_3_out, and_4_out, and_5_out, and_6_out, and_7_out, and_8_out, and_9_out,
       and_10_out, and_11_out, and_12_out, and_13_out, and_14_out, and_15_out, and_16_out, and_17_out,
       and_18_out, and_19_out, and_20_out, and_21_out, and_22_out, and_23_out, and_24_out, and_25_out,
       and_26_out, and_27_out, and_28_out, and_29_out, and_30_out, and_31_out, and_32_out, decoder_1_out0,
       decoder_1_out1, decoder_1_out2, decoder_1_out3, decoder_1_out4, decoder_1_out5, decoder_1_out6,
       decoder_1_out7, decoder_1_out8, decoder_1_out9, decoder_1_out10, decoder_1_out11, decoder_1_out12,
       decoder_1_out13, decoder_1_out14, decoder_1_out15, decoder_1_out16, decoder_1_out17, decoder_1_out18,
       decoder_1_out19, decoder_1_out20, decoder_1_out21, decoder_1_out22, decoder_1_out23, decoder_1_out24,
       decoder_1_out25, decoder_1_out26, decoder_1_out27, decoder_1_out28, decoder_1_out29, decoder_1_out30,
       decoder_1_out31;
  wire [31:0] _0_q, _1_q, _2_q, _3_q, _4_q, _5_q, _6_q, _7_q, _8_q, _9_q, _10_q, _11_q, _12_q, _13_q, _14_q,
       _15_q, _16_q, _17_q, _18_q, _19_q, _20_q, _21_q, _22_q, _23_q, _24_q, _25_q, _26_q, _27_q, _28_q,
       _29_q, _30_q, _31_q;

  Decoder #(.select(5), .enable("false")) decoder_1 (
    .out0(decoder_1_out0), .out1(decoder_1_out1), .out2(decoder_1_out2), .out3(decoder_1_out3),
    .out4(decoder_1_out4), .out5(decoder_1_out5), .out6(decoder_1_out6), .out7(decoder_1_out7),
    .out8(decoder_1_out8), .out9(decoder_1_out9), .out10(decoder_1_out10), .out11(decoder_1_out11),
    .out12(decoder_1_out12), .out13(decoder_1_out13), .out14(decoder_1_out14), .out15(decoder_1_out15),
    .out16(decoder_1_out16), .out17(decoder_1_out17), .out18(decoder_1_out18), .out19(decoder_1_out19),
    .out20(decoder_1_out20), .out21(decoder_1_out21), .out22(decoder_1_out22), .out23(decoder_1_out23),
    .out24(decoder_1_out24), .out25(decoder_1_out25), .out26(decoder_1_out26), .out27(decoder_1_out27),
    .out28(decoder_1_out28), .out29(decoder_1_out29), .out30(decoder_1_out30), .out31(decoder_1_out31),
    .sel(WriteReg));
  and and_1 (and_1_out, Write, decoder_1_out0);
  and and_2 (and_2_out, Write, decoder_1_out1);
  and and_3 (and_3_out, Write, decoder_1_out2);
  and and_4 (and_4_out, Write, decoder_1_out3);
  and and_5 (and_5_out, Write, decoder_1_out4);
  and and_6 (and_6_out, Write, decoder_1_out5);
  and and_7 (and_7_out, Write, decoder_1_out6);
  and and_8 (and_8_out, Write, decoder_1_out7);
  and and_9 (and_9_out, Write, decoder_1_out8);
  and and_10 (and_10_out, Write, decoder_1_out9);
  and and_11 (and_11_out, Write, decoder_1_out10);
  and and_12 (and_12_out, Write, decoder_1_out11);
  and and_13 (and_13_out, Write, decoder_1_out12);
  and and_14 (and_14_out, Write, decoder_1_out13);
  and and_15 (and_15_out, Write, decoder_1_out14);
  and and_16 (and_16_out, Write, decoder_1_out15);
  and and_17 (and_17_out, Write, decoder_1_out16);
  and and_18 (and_18_out, Write, decoder_1_out17);
  and and_19 (and_19_out, Write, decoder_1_out18);
  and and_20 (and_20_out, Write, decoder_1_out19);
  and and_21 (and_21_out, Write, decoder_1_out20);
  and and_22 (and_22_out, Write, decoder_1_out21);
  and and_23 (and_23_out, Write, decoder_1_out22);
  and and_24 (and_24_out, Write, decoder_1_out23);
  and and_25 (and_25_out, Write, decoder_1_out24);
  and and_26 (and_26_out, Write, decoder_1_out25);
  and and_27 (and_27_out, Write, decoder_1_out26);
  and and_28 (and_28_out, Write, decoder_1_out27);
  and and_29 (and_29_out, Write, decoder_1_out28);
  and and_30 (and_30_out, Write, decoder_1_out29);
  and and_31 (and_31_out, Write, decoder_1_out30);
  and and_32 (and_32_out, Write, decoder_1_out31);
  Register #(.width(32)) _0 (.D(WriteData), .en(and_1_out), .Q(_0_q), .clk(Clock));  // open: clr
  Register #(.width(32)) _1 (.D(WriteData), .en(and_2_out), .Q(_1_q), .clk(Clock));  // open: clr
  Register #(.width(32)) _2 (.D(WriteData), .en(and_3_out), .Q(_2_q), .clk(Clock));  // open: clr
  Register #(.width(32)) _3 (.D(WriteData), .en(and_4_out), .Q(_3_q), .clk(Clock));  // open: clr
  Register #(.width(32)) _4 (.D(WriteData), .en(and_5_out), .Q(_4_q), .clk(Clock));  // open: clr
  Register #(.width(32)) _5 (.D(WriteData), .en(and_6_out), .Q(_5_q), .clk(Clock));  // open: clr
  Register #(.width(32)) _6 (.D(WriteData), .en(and_7_out), .Q(_6_q), .clk(Clock));  // open: clr
  Register #(.width(32)) _7 (.D(WriteData), .en(and_8_out), .Q(_7_q), .clk(Clock));  // open: clr
  Register #(.width(32)) _8 (.D(WriteData), .en(and_9_out), .Q(_8_q), .clk(Clock));  // open: clr
  Register #(.width(32)) _9 (.D(WriteData), .en(and_10_out), .Q(_9_q), .clk(Clock));  // open: clr
  Register #(.width(32)) _10 (.D(WriteData), .en(and_11_out), .Q(_10_q), .clk(Clock));  // open: clr
  Register #(.width(32)) _11 (.D(WriteData), .en(and_12_out), .Q(_11_q), .clk(Clock));  // open: clr
  Register #(.width(32)) _12 (.D(WriteData), .en(and_13_out), .Q(_12_q), .clk(Clock));  // open: clr
  Register #(.width(32)) _13 (.D(WriteData), .en(and_14_out), .Q(_13_q), .clk(Clock));  // open: clr
  Register #(.width(32)) _14 (.D(WriteData), .en(and_15_out), .Q(_14_q), .clk(Clock));  // open: clr
  Register #(.width(32)) _15 (.D(WriteData), .en(and_16_out), .Q(_15_q), .clk(Clock));  // open: clr
  Register #(.width(32)) _16 (.D(WriteData), .en(and_17_out), .Q(_16_q), .clk(Clock));  // open: clr
  Register #(.width(32)) _17 (.D(WriteData), .en(and_18_out), .Q(_17_q), .clk(Clock));  // open: clr
  Register #(.width(32)) _18 (.D(WriteData), .en(and_19_out), .Q(_18_q), .clk(Clock));  // open: clr
  Register #(.width(32)) _19 (.D(WriteData), .en(and_20_out), .Q(_19_q), .clk(Clock));  // open: clr
  Register #(.width(32)) _20 (.D(WriteData), .en(and_21_out), .Q(_20_q), .clk(Clock));  // open: clr
  Register #(.width(32)) _21 (.D(WriteData), .en(and_22_out), .Q(_21_q), .clk(Clock));  // open: clr
  Register #(.width(32)) _22 (.D(WriteData), .en(and_23_out), .Q(_22_q), .clk(Clock));  // open: clr
  Register #(.width(32)) _23 (.D(WriteData), .en(and_24_out), .Q(_23_q), .clk(Clock));  // open: clr
  Register #(.width(32)) _24 (.D(WriteData), .en(and_25_out), .Q(_24_q), .clk(Clock));  // open: clr
  Register #(.width(32)) _25 (.D(WriteData), .en(and_26_out), .Q(_25_q), .clk(Clock));  // open: clr
  Register #(.width(32)) _26 (.D(WriteData), .en(and_27_out), .Q(_26_q), .clk(Clock));  // open: clr
  Register #(.width(32)) _27 (.D(WriteData), .en(and_28_out), .Q(_27_q), .clk(Clock));  // open: clr
  Register #(.width(32)) _28 (.D(WriteData), .en(and_29_out), .Q(_28_q), .clk(Clock));  // open: clr
  Register #(.width(32)) _29 (.D(WriteData), .en(and_30_out), .Q(_29_q), .clk(Clock));  // open: clr
  Register #(.width(32)) _30 (.D(WriteData), .en(and_31_out), .Q(_30_q), .clk(Clock));  // open: clr
  Register #(.width(32)) _31 (.D(WriteData), .en(and_32_out), .Q(_31_q), .clk(Clock));  // open: clr
  Multiplexer #(.select(5), .width(32), .enable("false")) multiplexer_1 (
    .in0(_0_q), .in1(_1_q), .in2(_2_q), .in3(_3_q), .in4(_4_q), .in5(_5_q), .in6(_6_q), .in7(_7_q),
    .in8(_8_q), .in9(_9_q), .in10(_10_q), .in11(_11_q), .in12(_12_q), .in13(_13_q), .in14(_14_q),
    .in15(_15_q), .in16(_16_q), .in17(_17_q), .in18(_18_q), .in19(_19_q), .in20(_20_q), .in21(_21_q),
    .in22(_22_q), .in23(_23_q), .in24(_24_q), .in25(_25_q), .in26(_26_q), .in27(_27_q), .in28(_28_q),
    .in29(_29_q), .in30(_30_q), .in31(_31_q), .out(ReadData_1), .sel(Read_Reg1));
  Multiplexer #(.select(5), .width(32), .enable("false")) multiplexer_2 (
    .in0(_0_q), .in1(_1_q), .in2(_2_q), .in3(_3_q), .in4(_4_q), .in5(_5_q), .in6(_6_q), .in7(_7_q),
    .in8(_8_q), .in9(_9_q), .in10(_10_q), .in11(_11_q), .in12(_12_q), .in13(_13_q), .in14(_14_q),
    .in15(_15_q), .in16(_16_q), .in17(_17_q), .in18(_18_q), .in19(_19_q), .in20(_20_q), .in21(_21_q),
    .in22(_22_q), .in23(_23_q), .in24(_24_q), .in25(_25_q), .in26(_26_q), .in27(_27_q), .in28(_28_q),
    .in29(_29_q), .in30(_30_q), .in31(_31_q), .out(ReadData_2), .sel(Read_Reg2));
endmodule

// IF
module Instruction_Fetch_Module (
  input  Clock,
  input  Enable,
  output [31:0] IR
);

  wire [31:0] adder_1_out, PC_q;

  Register #(.width(32)) PC (.D(adder_1_out), .Q(PC_q), .clk(Clock));  // open: en, clr
  Adder #(.width(32)) adder_1 (.a(32'h1), .b(PC_q), .out(adder_1_out));  // open: cin, cout
  RAM #(.addrWidth(24), .dataWidth(32)) ram_1 (
    .addr(PC_q[23:0]), .data(IR), .clk(Clock), .ld(Enable));  // open: sel, clr
endmodule

module ALU (
  input  [2:0] ALUOperation,
  input  [31:0] SRC1,
  input  [31:0] SRC2,
  output ZF,
  output [31:0] ALUResult
);

  wire [31:0] adder_1_out, adder_2_out, and_1_out, bit_extender_1_out, not_1_out, or_1_out;

  assign and_1_out = SRC1 & SRC2;  // AND_Gate and_1, 32 bits wide
  assign not_1_out = ~SRC2;  // NOT_Gate not_1, 32 bits wide
  assign or_1_out = SRC1 | SRC2;  // OR_Gate or_1, 32 bits wide
  Adder #(.width(32)) adder_1 (.a(SRC1), .b(SRC2), .out(adder_1_out));  // open: cin, cout
  Adder #(.width(32)) adder_2 (.a(SRC1), .b(not_1_out), .out(adder_2_out), .cin(1'b1));  // open: cout
  assign bit_extender_1_out = {{31{1'b0}}, adder_2_out[31]};  // Bit_Extender bit_extender_1
  Multiplexer #(.select(3), .width(32), .enable("false")) multiplexer_1 (
    .in0(and_1_out), .in1(or_1_out), .in2(adder_1_out), .in6(adder_2_out), .in7(bit_extender_1_out),
    .out(ALUResult), .sel(ALUOperation));  // open: in3, in4, in5
  Comparator #(.width(32)) comparator_1 (.a({32{1'b0}}), .b(ALUResult), .eq(ZF));  // open: gt, lt
endmodule

module DataMem (
  input  [31:0] Address,
  input  [31:0] Write_Data,
  input  MemRead,
  input  MemWrite,
  input  Clock,
  output [31:0] Read_Data
);

  RAM #(.addrWidth(24), .dataWidth(32), .bus("separate")) ram_1 (
    .addr(Address[23:0]), .din(Write_Data), .data(Read_Data), .str(MemWrite), .clk(Clock), .ld(MemRead));  // open: sel, clr
endmodule

module test_datamem (
  output [31:0] ReadData
);

  wire Clock_out;

  Clock Clock (.out(Clock_out));
  DataMem datamem_1 (
    .Address(32'h1), .Write_Data(32'habcd), .MemRead(1'b1), .MemWrite(1'b1), .Clock(Clock_out),
    .Read_Data(ReadData));

  // Notes on the sheet:
  //   Address
  //   WriteData
  //   Memread
  //   Memwrite
endmodule

module R_TYPE_INSTRUCTIONS (
  output [31:0] Readdata_1,
  output [31:0] IR,
  output [4:0] ReadReg1,
  output zero_flag,
  output [31:0] o_p,
  output [31:0] Readdata2,
  output [4:0] ReadReg2
);

  wire clock_1_out;

  Clock clock_1 (.out(clock_1_out));
  Instruction_Fetch_Module IF (.Clock(clock_1_out), .Enable(1'b1), .IR(IR));
  ReadPort RegFile (
    .Read_Reg1(IR[25:21]), .Read_Reg2(IR[20:16]), .Write(1'b1), .Clock(clock_1_out), .WriteReg(IR[15:11]),
    .WriteData(32'h2), .ReadData_1(Readdata_1), .ReadData_2(Readdata2));
  ALU ALU (.ALUOperation(3'b110), .SRC1(Readdata_1), .SRC2(Readdata2), .ZF(zero_flag), .ALUResult(o_p));

  assign ReadReg1 = IR[25:21];
  assign ReadReg2 = IR[20:16];

  // Notes on the sheet:
  //   Clock
  //   Enable
  //   WriteData
  //   Writesignal
  //   ALU OP
endmodule

module R_Lw_Sw (
  output zero_flag
);

  wire clock_1_out;
  wire [4:0] multiplexer_1_out;
  wire [31:0] alu_1_aluresult, bit_extender_1_out, datamem_1_read_data, instruction_fetch_module_1_ir,
       multiplexer_2_out, multiplexer_3_out, readport_1_readdata_1, readport_1_readdata_2;

  Clock clock_1 (.out(clock_1_out));
  Instruction_Fetch_Module instruction_fetch_module_1 (
    .Clock(clock_1_out), .Enable(1'b1), .IR(instruction_fetch_module_1_ir));
  // Probe on instruction_fetch_module_1_ir[20:16]
  // Probe on instruction_fetch_module_1_ir[25:21]
  // Probe on instruction_fetch_module_1_ir[15:0]
  // Probe on multiplexer_1_out
  Multiplexer #(.width(5)) multiplexer_1 (
    .in0(instruction_fetch_module_1_ir[20:16]), .in1(instruction_fetch_module_1_ir[15:11]),
    .out(multiplexer_1_out), .sel(1'b1));  // open: en
  assign bit_extender_1_out = {{16{1'b0}}, instruction_fetch_module_1_ir[15:0]};  // Bit_Extender bit_extender_1
  // Probe on readport_1_readdata_1
  ReadPort readport_1 (
    .Read_Reg1(instruction_fetch_module_1_ir[25:21]), .Read_Reg2(instruction_fetch_module_1_ir[20:16]),
    .Write(1'b1), .Clock(clock_1_out), .WriteReg(multiplexer_1_out), .WriteData(multiplexer_3_out),
    .ReadData_1(readport_1_readdata_1), .ReadData_2(readport_1_readdata_2));
  // Probe on readport_1_readdata_1
  // Probe on readport_1_readdata_2
  Multiplexer #(.width(32)) multiplexer_2 (
    .in0(readport_1_readdata_2), .in1(bit_extender_1_out), .out(multiplexer_2_out), .sel(1'b0));  // open: en
  // Probe on multiplexer_2_out
  ALU alu_1 (
    .ALUOperation(3'b010), .SRC1(readport_1_readdata_1), .SRC2(multiplexer_2_out), .ZF(zero_flag),
    .ALUResult(alu_1_aluresult));
  // Probe on multiplexer_3_out
  // Probe on alu_1_aluresult
  // Probe on readport_1_readdata_2
  // Probe on datamem_1_read_data
  DataMem datamem_1 (
    .Address(alu_1_aluresult), .Write_Data(readport_1_readdata_2), .MemRead(1'b0), .MemWrite(1'b0),
    .Clock(clock_1_out), .Read_Data(datamem_1_read_data));
  Multiplexer #(.width(32)) multiplexer_3 (
    .in0(alu_1_aluresult), .in1(datamem_1_read_data), .out(multiplexer_3_out), .sel(1'b0));  // open: en

  // Notes on the sheet:
  //   Clock
  //   Enable
  //   RegDst
  //   RegWrite
  //   ALUsrc
  //   MemRead
  //   MemWrite
  //   MemToReg
endmodule

// ACU
module ALU_CU (
  input  [1:0] ALUOP,
  input  [5:0] FC,
  output [2:0] out_3
);

  wire and_1_out, or_1_out;

  and and_1 (and_1_out, ALUOP[1], FC[1]);
  or or_1 (or_1_out, FC[3], FC[0]);
  and and_2 (out_3[0], ALUOP[1], or_1_out);
  or or_2 (out_3[2], ALUOP[0], and_1_out);
  nand nand_1 (out_3[1], FC[2], ALUOP[1]);

  // Notes on the sheet:
  //   A2
  //   A1
  //   A0
endmodule

// Main cu
module Main_CU (
  input  [5:0] OPCODES,
  output RegWrite,
  output ALUsrc,
  output MemRead,
  output Branch,
  output ALUOp1,
  output RegDst,
  output MemtoReg,
  output MemWrite,
  output Jump,
  output ALUOp0
);

  wire not_1_out, not_2_out, not_3_out, not_4_out, not_5_out, not_6_out;

  not not_1 (not_1_out, OPCODES[5]);
  not not_2 (not_2_out, OPCODES[4]);
  not not_3 (not_3_out, OPCODES[3]);
  not not_4 (not_4_out, OPCODES[2]);
  not not_5 (not_5_out, OPCODES[1]);
  not not_6 (not_6_out, OPCODES[0]);
  and R (ALUOp1, not_6_out, not_5_out, not_4_out, not_3_out, not_2_out, not_1_out);
  and lw (MemRead, OPCODES[0], OPCODES[1], not_4_out, not_3_out, not_2_out, OPCODES[5]);
  and sw (MemWrite, OPCODES[0], OPCODES[1], not_4_out, OPCODES[3], not_2_out, OPCODES[5]);
  and beq (ALUOp0, not_6_out, not_5_out, OPCODES[2], not_3_out, not_2_out, not_1_out);
  and j (Jump, not_6_out, OPCODES[1], not_4_out, not_3_out, not_2_out, not_1_out);
  or or_1 (RegWrite, ALUOp1, MemRead);
  or or_2 (ALUsrc, MemRead, MemWrite);

  assign Branch = ALUOp0;
  assign MemtoReg = MemRead;
  assign RegDst = ALUOp1;
endmodule

module COMPLETE_SCDP (
  output zero_flag
);

  wire ALUOp0, ALUOp1, ALUsrc, Branch, clock_1_out, Jump, MemRead, MemtoReg, MemWrite, RegDst, RegWrite;
  wire [2:0] Apins;
  wire [4:0] multiplexer_1_out;
  wire [5:0] instruction_fetch_module_1_ir_2;
  wire [25:0] instruction_fetch_module_1_ir;
  wire [31:0] alu_1_aluresult, bit_extender_1_out, datamem_1_read_data, multiplexer_2_out, multiplexer_3_out,
       readport_1_readdata_1, readport_1_readdata_2;

  Clock clock_1 (.out(clock_1_out));
  Main_CU main_cu_1 (
    .OPCODES(instruction_fetch_module_1_ir_2), .RegWrite(RegWrite), .RegDst(RegDst), .ALUsrc(ALUsrc),
    .MemtoReg(MemtoReg), .MemRead(MemRead), .MemWrite(MemWrite), .Branch(Branch), .Jump(Jump),
    .ALUOp1(ALUOp1), .ALUOp0(ALUOp0));
  Instruction_Fetch_Module instruction_fetch_module_1 (
    .Clock(clock_1_out), .Enable(1'b1), .IR({instruction_fetch_module_1_ir_2, instruction_fetch_module_1_ir}));
  // Probe on instruction_fetch_module_1_ir[20:16]
  // Probe on instruction_fetch_module_1_ir[25:21]
  // Probe on instruction_fetch_module_1_ir[15:0]
  // Probe on multiplexer_1_out
  Multiplexer #(.width(5)) multiplexer_1 (
    .in0(instruction_fetch_module_1_ir[20:16]), .in1(instruction_fetch_module_1_ir[15:11]),
    .out(multiplexer_1_out), .sel(RegDst));  // open: en
  assign bit_extender_1_out = {{16{1'b0}}, instruction_fetch_module_1_ir[15:0]};  // Bit_Extender bit_extender_1
  ALU_CU alu_cu_1 (.ALUOP({ALUOp1, ALUOp0}), .FC(instruction_fetch_module_1_ir[5:0]), .out_3(Apins));
  // Probe on readport_1_readdata_1
  ReadPort readport_1 (
    .Read_Reg1(instruction_fetch_module_1_ir[25:21]), .Read_Reg2(instruction_fetch_module_1_ir[20:16]),
    .Write(RegWrite), .Clock(clock_1_out), .WriteReg(multiplexer_1_out), .WriteData(multiplexer_3_out),
    .ReadData_1(readport_1_readdata_1), .ReadData_2(readport_1_readdata_2));
  // Probe on readport_1_readdata_1
  // Probe on readport_1_readdata_2
  Multiplexer #(.width(32)) multiplexer_2 (
    .in0(readport_1_readdata_2), .in1(bit_extender_1_out), .out(multiplexer_2_out), .sel(ALUsrc));  // open: en
  // Probe on multiplexer_2_out
  ALU alu_1 (
    .ALUOperation(Apins), .SRC1(readport_1_readdata_1), .SRC2(multiplexer_2_out), .ZF(zero_flag),
    .ALUResult(alu_1_aluresult));
  // Probe on multiplexer_3_out
  // Probe on alu_1_aluresult
  // Probe on readport_1_readdata_2
  // Probe on datamem_1_read_data
  DataMem datamem_1 (
    .Address(alu_1_aluresult), .Write_Data(readport_1_readdata_2), .MemRead(MemRead), .MemWrite(MemWrite),
    .Clock(clock_1_out), .Read_Data(datamem_1_read_data));
  Multiplexer #(.width(32)) multiplexer_3 (
    .in0(alu_1_aluresult), .in1(datamem_1_read_data), .out(multiplexer_3_out), .sel(MemtoReg));  // open: en

  // Notes on the sheet:
  //   Clock
  //   Enable
endmodule
